// Logisim project SA.circ as structural Verilog: 3 circuits, main circuit main
module main (
);

  wire clock_1_out, comparator_1_eq, comparator_1_gt, firsttestcell_1_reset_thru, nor_1_out, not_1_out,
       shift_register_1_q0, shift_register_1_q1, shift_register_1_q2, shift_register_1_q3,
       shift_register_1_q4, shift_register_1_q5, shift_register_1_q6, shift_register_1_q7,
       testcell_1_reset_thru, testcell_2_reset_thru, testcell_3_reset_thru, testcell_4_reset_thru,
       testcell_5_reset_thru;
  wire [7:0] d_ff_1_q, or_1_out, register_1_q;

  Clock clock_1 (.out(clock_1_out));
  not not_1 (not_1_out, clock_1_out);
  FirstTestCell firsttestcell_1 (
    .Reset(shift_register_1_q0), .Reset_Thru(firsttestcell_1_reset_thru), .Test(shift_register_1_q1),
    .Komp(or_1_out[0]), .CLK(clock_1_out), .TestOut(d_ff_1_q[7]), .DataOut(or_1_out[7]));
  Shift_Register shift_register_1 (
    .in(nor_1_out), .clk(not_1_out), .q0(shift_register_1_q0), .q1(shift_register_1_q1),
    .q2(shift_register_1_q2), .q3(shift_register_1_q3), .q4(shift_register_1_q4), .q5(shift_register_1_q5),
    .q6(shift_register_1_q6), .q7(shift_register_1_q7));  // open: shift, out, load, clr, d0, d1, d2, d3, d4, d5, d6, d7
  TestCell testcell_1 (
    .Reset(testcell_2_reset_thru), .Reset_Thru(testcell_1_reset_thru), .Test(shift_register_1_q3),
    .Komp(or_1_out[0]), .CLK(clock_1_out), .TestOut(d_ff_1_q[5]), .DataOut(or_1_out[5]));
  TestCell testcell_2 (
    .Reset(firsttestcell_1_reset_thru), .Reset_Thru(testcell_2_reset_thru), .Test(shift_register_1_q2),
    .Komp(or_1_out[0]), .CLK(clock_1_out), .TestOut(d_ff_1_q[6]), .DataOut(or_1_out[6]));
  TestCell testcell_3 (
    .Reset(testcell_1_reset_thru), .Reset_Thru(testcell_3_reset_thru), .Test(shift_register_1_q4),
    .Komp(or_1_out[0]), .CLK(clock_1_out), .TestOut(d_ff_1_q[4]), .DataOut(or_1_out[4]));
  D_Flip_Flop d_ff_1 (.clk(not_1_out), .D(shift_register_1_q7), .Q(d_ff_1_q[0]));  // open: Qn, preset, en, reset
  TestCell testcell_4 (
    .Reset(testcell_3_reset_thru), .Reset_Thru(testcell_4_reset_thru), .Test(shift_register_1_q5),
    .Komp(or_1_out[0]), .CLK(clock_1_out), .TestOut(d_ff_1_q[3]), .DataOut(or_1_out[3]));
  Comparator #(.mode("unsigned")) comparator_1 (
    .a({8{1'b0}}), .b(d_ff_1_q), .gt(comparator_1_gt), .eq(comparator_1_eq));  // open: lt
  nor nor_1 (nor_1_out, shift_register_1_q7, shift_register_1_q6, shift_register_1_q5, shift_register_1_q4, shift_register_1_q3, shift_register_1_q2, shift_register_1_q1, shift_register_1_q0);
  TestCell testcell_5 (
    .Reset(testcell_4_reset_thru), .Reset_Thru(testcell_5_reset_thru), .Test(shift_register_1_q6),
    .Komp(or_1_out[0]), .CLK(clock_1_out), .TestOut(d_ff_1_q[2]), .DataOut(or_1_out[2]));
  TestCell testcell_6 (
    .Reset(testcell_5_reset_thru), .Test(shift_register_1_q7), .Komp(or_1_out[0]), .CLK(clock_1_out),
    .TestOut(d_ff_1_q[1]), .DataOut(or_1_out[1]));  // open: Reset_Thru
  or or_1 (or_1_out[0], comparator_1_gt, comparator_1_eq);
  LED led_1 (.in(or_1_out[0]));
  Register register_1 (.D(or_1_out), .en(d_ff_1_q[0]), .Q(register_1_q), .clk(clock_1_out));  // open: clr
  // Probe on register_1_q

  // Notes on the sheet:
  //   VIN
  //   "ANALOG SECTION"
  //   <- "DAC"
endmodule

module TestCell (
  input  Komp,
  input  Test,
  input  CLK,
  input  Reset,
  output Reset_Thru,
  output TestOut,
  output DataOut
);

  wire and_1_out, multiplexer_1_out, not_1_out, or_1_out;

  not not_1 (not_1_out, Reset);
  and and_1 (and_1_out, Komp, not_1_out);
  or or_1 (or_1_out, Test, Reset);
  or or_2 (TestOut, Test, DataOut);
  D_Flip_Flop d_ff_1 (.clk(CLK), .D(multiplexer_1_out), .Q(DataOut));  // open: Qn, preset, en, reset
  Multiplexer #(.enable("false")) multiplexer_1 (
    .in0(DataOut), .in1(and_1_out), .out(multiplexer_1_out), .sel(or_1_out));

  assign Reset_Thru = Reset;

  // Notes on the sheet:
  //   Using MUX to enable/disable FF because IC I will be using has no Enable per bit
endmodule

module FirstTestCell (
  input  Test,
  input  Komp,
  input  CLK,
  input  Reset,
  output Reset_Thru,
  output TestOut,
  output DataOut
);

  wire multiplexer_1_out;

  Multiplexer multiplexer_1 (.in0(DataOut), .in1(Komp), .out(multiplexer_1_out), .sel(Test));  // open: en
  or or_1 (TestOut, Test, DataOut);
  D_Flip_Flop d_ff_1 (.clk(CLK), .D(multiplexer_1_out), .Q(DataOut));  // open: Qn, preset, en, reset

  assign Reset_Thru = Reset;
endmodule
